# Fritzing sketch 1bef67b673c7c30e2fe50f0ee74fd02f (saved by Fritzing 0.9.3b)
circuit board: 16.9387cm x 10.6565cm
breadboards: 1

parts:
  R1 = Rotary Potentiometer (Small) [maximum_resistance=100kΩ package=THT]
  R3 = Rotary Potentiometer (Small) [maximum_resistance=100kΩ package=THT]
  R4 = Rotary Potentiometer (Small) [maximum_resistance=100kΩ package=THT]
  IC1 = MCP3008 [part_number=MCP3008]
  R2 = Rotary Potentiometer (Small) [maximum_resistance=100kΩ package=THT]
  Raspberry_Pi_1 = Raspberry Pi 3 [part_number=RPI-3-V1.2]
  J1 = shrouded pin header, 10 pins [form="♂ (shrouded male)"]  # not connected

nets (from the schematic view):
  N1: R1.leg1, R3.leg2, R4.leg2, IC1.connector9, IC1.connector14, R2.leg2, Raspberry_Pi_1.GND
  N2: R1.wiper, IC1.connector3
  3V3: R1.leg2, R3.leg1, R4.leg1, IC1.connector15, IC1.connector16, R2.leg1, Raspberry_Pi_1.3v3, Raspberry_Pi_1.3V3
  N3: R3.wiper, IC1.connector1
  N4: R4.wiper, IC1.connector4
  N5: IC1.connector2, R2.wiper
  N6: IC1.connector10, Raspberry_Pi_1.GPIO25
  N7: IC1.connector13, Raspberry_Pi_1.GPIO18
